# Fritzing sketch RGB Clock (saved by Fritzing 0.9.0b)
circuit board: 5.26907cm x 5.78068cm

parts:
  Part1 = Arduino Pro Mini v13
  Part2 = Real Time Clock Module - DS1307 RTC Breakout Board
  JP2 = Header 6 [package=molex-1x6-ra]
  NEOPIXEL1 = Neopixel Strip -- Black (60/m)

nets:
  N1: Part1.DTR, JP2.6
  N2: Part1.D0/TX, JP2.5
  N3: Part1.D1/RX, JP2.4
  N4: Part1.VCC, JP2.3
  GND: Part1.GND, Part2.GND, JP2.1, JP2.2, NEOPIXEL1.GND
  N5: Part1.A4, Part2.SDA
  N6: Part1.A5, Part2.SQW, Part2.SCL
  N7: Part1.D6_PWM, NEOPIXEL1.+5V
  N8: Part2.5V, NEOPIXEL1.DI

custom parts:
  Neopixel Strip -- Black (60/m): Neopixel Strip, Black, 60 pixels per meter.
